// Logisim project main.circ as structural Verilog: 2 circuits, main circuit main
module main (
  input  [15:0] user_input,
  output [15:0] main_output,
  output [3:0] output_index
);

  wire alu_1_is_equal, alu_1_is_greater, alu_1_is_shorter, clk_out, uc_1_enable_bus_mux_output,
       uc_1_enable_change_acc, uc_1_enable_change_ir, uc_1_enable_change_pc, uc_1_enable_change_ram,
       uc_1_enable_output_ram, uc_1_enable_print, uc_1_load_pc, uc_1_mux_input_acc, uc_1_mux_input_ram,
       uc_1_op_alu, uc_1_pc_counter_is_up;
  wire [0:0] alu_1_overflow;
  wire [1:0] uc_1_mux_output_ram;
  wire [3:0] IR_q_2;
  wire [11:0] IR_q, multiplexer_1_out, PC_q;
  wire [15:0] ACC_q, alu_1_result, multiplexer_2_out, ram_1_data;

  Clock clk (.out(clk_out));
  Counter #(.width(12), .max('hfff)) PC (
    .clr(1'b0), .load(uc_1_load_pc), .up(uc_1_pc_counter_is_up), .count(uc_1_enable_change_pc),
    .clk(clk_out), .D(IR_q), .Q(PC_q));  // open: carry
  UC uc_1 (
    .clk(clk_out), .instruction(IR_q_2), .is_greater(alu_1_is_greater), .is_equal(alu_1_is_equal),
    .is_shorter(alu_1_is_shorter), .mux_input_acc(uc_1_mux_input_acc), .enable_print(uc_1_enable_print),
    .op_alu(uc_1_op_alu), .mux_output_ram(uc_1_mux_output_ram), .enable_change_acc(uc_1_enable_change_acc),
    .enable_change_ir(uc_1_enable_change_ir), .enable_change_ram(uc_1_enable_change_ram),
    .enable_output_ram(uc_1_enable_output_ram), .mux_input_ram(uc_1_mux_input_ram), .load_PC(uc_1_load_pc),
    .enable_change_PC(uc_1_enable_change_pc), .pc_counter_is_up(uc_1_pc_counter_is_up),
    .enable_bus_mux_output(uc_1_enable_bus_mux_output));
  Register #(.width(16)) IR (.D(ram_1_data), .en(uc_1_enable_change_ir), .clk(clk_out), .Q({IR_q_2, IR_q}), .clr(1'b0));
  ALU alu_1 (
    .OP(uc_1_op_alu), .a(ACC_q), .b(ram_1_data), .result(alu_1_result), .Overflow(alu_1_overflow[0]),
    .is_equal(alu_1_is_equal), .is_greater(alu_1_is_greater), .is_shorter(alu_1_is_shorter));
  Multiplexer #(.width(12), .enable("false")) multiplexer_1 (
    .in0(PC_q), .in1(IR_q), .out(multiplexer_1_out), .sel(uc_1_mux_input_ram));
  Multiplexer #(.width(16), .enable("false")) multiplexer_2 (
    .in0(ram_1_data), .in1(alu_1_result), .out(multiplexer_2_out), .sel(uc_1_mux_input_acc));
  Register #(.width(16)) ACC (.D(multiplexer_2_out), .en(uc_1_enable_change_acc), .clk(clk_out), .Q(ACC_q), .clr(1'b0));
  RAM #(.addrWidth(12), .dataWidth(16), .trigger("high")) ram_1 (
    .addr(multiplexer_1_out), .we(uc_1_enable_change_ram), .oe(uc_1_enable_output_ram), .data(ram_1_data));
  Multiplexer #(.select(2), .width(16), .disabled("Z")) multiplexer_3 (
    .in0({16{1'b0}}), .in1(ACC_q), .in2(user_input), .in3({{15{1'b0}}, alu_1_overflow[0]}), .out(ram_1_data),
    .sel(uc_1_mux_output_ram), .en(uc_1_enable_bus_mux_output));
  Register #(.width(16)) register_1 (
    .D(ram_1_data), .en(uc_1_enable_print), .clk(clk_out), .Q(main_output), .clr(1'b0));
  Counter #(.width(4), .max('hf)) counter_1 (
    .clr(1'b0), .load(1'b0), .up(1'b1), .count(uc_1_enable_print), .clk(clk_out), .Q(output_index));  // open: D, carry

  // Notes on the sheet:
  //   CPU unsigned 16 bit with 12 bit addresses
  //   operation
  //   address
  //   overflow
endmodule

module UC (
  input  clk,
  input  [3:0] instruction,
  input  is_greater,
  input  is_equal,
  input  is_shorter,
  output mux_input_acc,
  output enable_print,
  output op_alu,
  output [1:0] mux_output_ram,
  output enable_change_acc,
  output enable_change_ir,
  output enable_change_ram,
  output enable_output_ram,
  output mux_input_ram,
  output load_PC,
  output enable_change_PC,
  output pc_counter_is_up,
  output enable_bus_mux_output
);

  wire t_ff_1_q, t_ff_1_qn;
  wire [3:0] multiplexer_1_out;

  T_Flip_Flop #(.trigger("falling")) t_ff_1 (.T(1'b1), .clk(clk), .Q(t_ff_1_q), .Qn(t_ff_1_qn));  // open: reset, preset
  Multiplexer #(.width(4), .enable("false")) multiplexer_1 (
    .in0(4'b0101), .in1(instruction), .out(multiplexer_1_out), .sel(t_ff_1_qn));
  Multiplexer #(.select(4), .width(14), .enable("false")) multiplexer_2 (
    .in0({14{1'b0}}), .in1(14'h130), .in2(14'h251), .in3(14'h2130), .in4(14'h2930), .in5(14'ha6),
    .in6({14{1'b0}}), .in7(14'h451), .in8(14'h1030), .in9(14'h4), .in10(14'hc),
    .in11({{10{1'b0}}, {2{is_greater}}, 2'b01}), .in12({14{1'b0}}),
    .in13({{10{1'b0}}, {2{is_equal}}, 2'b01}), .in14({14{1'b0}}),
    .in15({{10{1'b0}}, {2{is_shorter}}, 2'b01}),
    .out({mux_input_acc, enable_print, op_alu, mux_output_ram, enable_change_acc, enable_change_ir, enable_change_ram, enable_output_ram, mux_input_ram, load_PC, enable_change_PC, pc_counter_is_up, enable_bus_mux_output}),
    .sel(multiplexer_1_out));

  // Notes on the sheet:
  //   fetch
  //   fetch phase
  //   instruction phase
  //   Jump to  to EE if [ACC] > 0
  //   Jump to EE if [ACC]=0
  //   Jump to EE if [ACC] < 0
  //   Jump to  to EE if [ACC] > 0
  //   Jump to EE if [ACC]=0
  //   Jump to EE if [ACC] < 0
  //   Store sum [ACC] with [EE] in ACC
  //   Store [ACC] subtracted by [EE] in ACC
  //   ------------------------- FETCH ---------------------
  //   Read number and store in EE
  //   Print [EE]
  //   Stop
  //   Jump to EE
  //   ----
  //   ----
  //   no operation
  //   Copy [EE] to ACC
  //   Copy [ACC] to EE
  //   ----
endmodule
